# Fritzing sketch sketch (saved by Fritzing 0.9.3b)
circuit board: 12.4135cm x 5.57931cm
breadboards: 1

parts:
  NodeMCU = NodeMCU V1.0
  DHT11 = DHT11 Humitidy and Temperature Sensor
  MQ-09 = MQ-9 breakout
  LM317 = Voltage Regulator [package=to220-adj]
  C1 = Electrolytic Capacitor [capacitance=220µF voltage=10V package="0405 [SMD, electrolytic]"]
  C2 = Electrolytic Capacitor [capacitance=10µF package="0405 [SMD, electrolytic]"]
  R1 = Resistor [tolerance=±5% resistance=390 package="0805 [SMD]"]
  R2 = Resistor [tolerance=±5% resistance=240 package="1206 [SMD]"]
  VCC1 = 4 x AAA Battery Mount

nets:
  GND: NodeMCU.GND, MQ-09.GND
  N1: NodeMCU.D6, DHT11.DATA
  N2: NodeMCU.Vin, LM317.OUT, C2.+, R2.Pin_0
  N3: NodeMCU.A0, MQ-09.AO
  VDD: DHT11.VDD, MQ-09.VCC, LM317.IN, C1.+, VCC1.+
  N4: DHT11.GND, C1.-, C2.-, R1.Pin_1, VCC1.-
  N5: LM317.ADJ, R1.Pin_0, R2.Pin_1

custom parts:
  NodeMCU V1.0: ESP8266 based NodeMCU
  DHT11 Humitidy and Temperature Sensor: DHT11 Humidity and Temperature Sensor
  MQ-9 breakout: SKU: 101284
